// Logisim project cpu.circ as structural Verilog: 1 circuit, main circuit main
module main (
  input  [31:0] INSTRUCTION,
  input  CLOCK,
  output [31:0] FETCH_ADDRESS,
  output [31:0] s0_Value,
  output [31:0] s1_Value,
  output [31:0] s2_Value,
  output [31:0] ra_Value,
  output [31:0] sp_Value
);

  wire add, add_op, addi, addiu, addu, addu_op, ALUSrc, \and , and_1_out, and_8_out, and_9_out, and_op, andi,
       beq, bne, branch_Result, comparator_2_eq, comparator_5_eq, comparator_6_eq, comparator_12_eq,
       comparator_15_eq, comparator_17_eq, comparator_20_eq, comparator_21_eq, comparator_22_eq,
       comparator_23_eq, comparator_26_eq, comparator_27_eq, equal, Extop, j, jal, jr, jump_sel, lui, lw,
       main_2_signed_overflow, MemWr, not_1_out, \or , or_1_out, or_5_out, or_6_out, or_7_out, or_8_out,
       or_9_out, or_10_out, or_11_out, or_12_out, or_13_out, or_15_out, or_16_out, or_17_out, or_18_out,
       or_26_out, or_27_out, or_28_out, or_30_out, or_31_out, or_32_out, or_33_out, or_op, ori, RegWr, rtype,
       shamtCtr, sll, slt, slt_op, slti, sltiu, sltu, sltu_op, sra, srl, sub, subu, sw, swinc;
  wire [1:0] adder_8_out, branch_sel, jr_sele, jump_sele, multiplexer_2_out, pc_selector, RegDst;
  wire [2:0] adder_9_out, adder_10_out, jar_sel, lui_sel, megtoreg_sele, swinc_sele, wb_selector;
  wire [3:0] add_sel, adder_3_out, adder_4_out, adder_5_out, adder_6_out, adder_7_out, adder_11_out,
       adder_12_out, adder_15_out, addu_sel, ALUctl, and_sel, or_sel, slt_sel, sltu_sel, sra_sel, srl_sel,
       sub_sel, subu_sel;
  wire [4:0] multiplexer_1_out, multiplexer_3_out;
  wire [5:0] funct;
  wire [15:6] imm16;
  wire [25:16] Jtype26;
  wire [27:0] pc_4;
  wire [31:0] bit_extender_1_out, bit_extender_2_out, busA_rs, busb, imm_after_shift, imm_result,
       main_2_result, main_3_p5, multiplexer_5_out, multiplexer_14_out, multiplexer_15_out,
       multiplexer_16_out, multiplexer_27_out, swinc_rs_imm16, upper;
  wire [31:16] imm_ext;
  wire [31:26] new_instruction;
  wire [31:28] jump_addr;

  // Probe on MemWr
  // Probe on busb
  // Probe on Extop
  Multiplexer #(.select(2), .width(5)) multiplexer_1 (
    .in0(imm16[15:11]), .in1(Jtype26[20:16]), .in2(Jtype26[25:21]), .out(multiplexer_1_out), .sel(RegDst));  // open: in3, en
  // Probe on jal
  // Probe on FETCH_ADDRESS
  Multiplexer #(.width(2)) multiplexer_2 (.in0(2'b01), .in1(2'b00), .out(multiplexer_2_out), .sel(rtype));  // open: en
  // Probe on Jtype26[25:21]
  // Probe on busA_rs
  // Probe on RegWr
  Multiplexer #(.width(5)) multiplexer_3 (
    .in0(multiplexer_1_out), .in1({5{1'b1}}), .out(multiplexer_3_out), .sel(jal));  // open: en
  Multiplexer #(.width(16)) multiplexer_4 (
    .in0({16{1'b0}}), .in1({16{1'b1}}), .out(imm_ext), .sel(and_1_out));  // open: en
  and and_1 (and_1_out, Extop, imm16[15]);
  Multiplexer #(.select(2), .width(32)) multiplexer_5 (
    .in0({jump_addr, pc_4}), .in1(imm_result), .in2({jump_addr, Jtype26, imm16, funct, 2'b00}),
    .in3(busA_rs), .out(multiplexer_5_out), .sel(pc_selector));  // open: en
  Adder #(.width(32)) adder_1 (.a(FETCH_ADDRESS), .b(32'h4), .out({jump_addr, pc_4}));  // open: cin, cout
  Multiplexer #(.width(2)) multiplexer_6 (.in0(multiplexer_2_out), .in1(2'b10), .out(RegDst), .sel(swinc));  // open: en
  or or_1 (or_1_out, sll, sra);
  or or_2 (shamtCtr, or_1_out, srl);
  or or_3 (jump_sel, j, jal);
  or or_4 (MemWr, sw, swinc);
  Comparator #(.width(6), .mode("unsigned")) comparator_1 (
    .a(new_instruction), .b({6{1'b0}}), .eq(rtype));  // open: gt, lt
  assign bit_extender_1_out = {{16{1'b0}}, {imm16, funct}};  // Bit_Extender bit_extender_1
  or or_5 (or_5_out, addi, addiu);
  or or_6 (or_6_out, or_5_out, or_7_out);
  or or_7 (or_7_out, lw, slti);
  or or_8 (or_8_out, sltiu, sw);
  or or_9 (or_9_out, or_8_out, swinc);
  or or_10 (or_10_out, addi, addiu);
  or or_11 (or_11_out, andi, lui);
  or or_12 (or_12_out, lw, ori);
  or or_13 (or_13_out, slti, sltiu);
  and and_2 (add, rtype, comparator_2_eq);
  Comparator #(.width(6), .mode("unsigned")) comparator_2 (
    .a(funct), .b(6'b100000), .eq(comparator_2_eq));  // open: gt, lt
  Comparator #(.width(6), .mode("unsigned")) comparator_3 (
    .a(new_instruction), .b(6'b001000), .eq(addi));  // open: gt, lt
  Comparator #(.width(6), .mode("unsigned")) comparator_4 (
    .a(new_instruction), .b(6'b001001), .eq(addiu));  // open: gt, lt
  and and_3 (addu, rtype, comparator_5_eq);
  Comparator #(.width(6), .mode("unsigned")) comparator_5 (
    .a(funct), .b(6'b100001), .eq(comparator_5_eq));  // open: gt, lt
  and and_4 (\and , rtype, comparator_6_eq);
  Comparator #(.width(6), .mode("unsigned")) comparator_6 (
    .a(funct), .b(6'b100100), .eq(comparator_6_eq));  // open: gt, lt
  Comparator #(.width(6), .mode("unsigned")) comparator_7 (
    .a(new_instruction), .b(6'b001100), .eq(andi));  // open: gt, lt
  Comparator #(.width(6), .mode("unsigned")) comparator_8 (
    .a(new_instruction), .b(6'b000100), .eq(beq));  // open: gt, lt
  Comparator #(.width(6), .mode("unsigned")) comparator_9 (
    .a(new_instruction), .b(6'b000101), .eq(bne));  // open: gt, lt
  Comparator #(.width(6), .mode("unsigned")) comparator_10 (
    .a(new_instruction), .b(6'b000010), .eq(j));  // open: gt, lt
  Comparator #(.width(6)) comparator_11 (.a(new_instruction), .b(6'b000011), .eq(jal));  // open: gt, lt
  and and_5 (jr, rtype, comparator_12_eq);
  Comparator #(.width(6), .mode("unsigned")) comparator_12 (
    .a(funct), .b(6'b001000), .eq(comparator_12_eq));  // open: gt, lt
  Comparator #(.width(6), .mode("unsigned")) comparator_13 (
    .a(new_instruction), .b(6'b001111), .eq(lui));  // open: gt, lt
  Comparator #(.width(6), .mode("unsigned")) comparator_14 (
    .a(new_instruction), .b(6'b100011), .eq(lw));  // open: gt, lt
  and and_6 (\or , rtype, comparator_15_eq);
  Comparator #(.width(6), .mode("unsigned")) comparator_15 (
    .a(funct), .b(6'b100101), .eq(comparator_15_eq));  // open: gt, lt
  Comparator #(.width(6), .mode("unsigned")) comparator_16 (
    .a(new_instruction), .b(6'b001101), .eq(ori));  // open: gt, lt
  and and_7 (slt, rtype, comparator_17_eq);
  Comparator #(.width(6), .mode("unsigned")) comparator_17 (
    .a(funct), .b(6'b101010), .eq(comparator_17_eq));  // open: gt, lt
  Comparator #(.width(6), .mode("unsigned")) comparator_18 (
    .a(new_instruction), .b(6'b001010), .eq(slti));  // open: gt, lt
  Comparator #(.width(6), .mode("unsigned")) comparator_19 (
    .a(new_instruction), .b(6'b001011), .eq(sltiu));  // open: gt, lt
  // Probe on Jtype26[20:16]
  // Probe on imm16[15:11]
  // Probe on RegDst
  // Probe on ALUctl
  Register #(.width(32)) PC (.D(multiplexer_5_out), .Q(FETCH_ADDRESS), .clk(CLOCK));  // open: en, clr
  // Probe on {jump_addr, pc_4}
  Shifter #(.width(32)) shifter_1 (.in(bit_extender_1_out), .\dist (5'b10000), .out(upper));
  or or_14 (Extop, or_6_out, or_9_out);
  or or_15 (or_15_out, or_10_out, or_11_out);
  or or_16 (or_16_out, or_12_out, or_13_out);
  // Probe on imm16[10:6]
  // Probe on RegWr
  regfile_main main_1 (
    .Read_Register_1(Jtype26[25:21]), .Read_Register_2(Jtype26[20:16]), .Write_Register(multiplexer_3_out),
    .Write_Data(multiplexer_27_out), .Write_Enable(RegWr), .Clock(CLOCK), .Read_Data_1(busA_rs),
    .Read_Data_2(busb), .s0_Value(s0_Value), .s1_Value(s1_Value), .s2_Value(s2_Value), .ra_Value(ra_Value),
    .sp_Value(sp_Value));
  or or_17 (or_17_out, or_15_out, or_16_out);
  or or_18 (or_18_out, sw, swinc);
  // Probe on funct
  // Probe on {imm16, funct}
  // Probe on ALUSrc
  or or_19 (add_op, add, addi);
  or or_20 (addu_op, addiu, addu);
  or or_21 (and_op, \and , andi);
  or or_22 (slt_op, slt, slti);
  or or_23 (sltu_op, sltiu, sltu);
  or or_24 (or_op, \or , ori);
  or or_25 (ALUSrc, or_17_out, or_18_out);
  Multiplexer #(.width(2)) multiplexer_7 (.in0(2'b00), .in1(2'b01), .out(branch_sel), .sel(branch_Result));  // open: en
  Multiplexer #(.width(2)) multiplexer_8 (.in0(2'b00), .in1(2'b10), .out(jump_sele), .sel(jump_sel));  // open: en
  Multiplexer #(.width(2)) multiplexer_9 (.in0(2'b00), .in1(2'b11), .out(jr_sele), .sel(jr));  // open: en
  Multiplexer #(.width(3)) multiplexer_10 (.in0(3'b000), .in1(3'b001), .out(lui_sel), .sel(lui));  // open: en
  Multiplexer #(.width(3)) multiplexer_11 (.in0(3'b000), .in1(3'b010), .out(megtoreg_sele), .sel(lw));  // open: en
  Multiplexer #(.width(3)) multiplexer_12 (.in0(3'b000), .in1(3'b011), .out(swinc_sele), .sel(swinc));  // open: en
  Multiplexer #(.width(3)) multiplexer_13 (.in0(3'b000), .in1(3'b100), .out(jar_sel), .sel(jal));  // open: en
  // Probe on new_instruction
  // Probe on shamtCtr
  // Probe on upper
  Multiplexer #(.width(32)) multiplexer_14 (
    .in0(busb), .in1({imm_ext, imm16, funct}), .out(multiplexer_14_out), .sel(ALUSrc));  // open: en
  // Probe on {imm_ext, imm16, funct}
  Adder #(.width(32)) adder_2 (.a({imm_ext, imm16, funct}), .b(busA_rs), .out(swinc_rs_imm16));  // open: cin, cout
  // Probe on INSTRUCTION
  or or_26 (or_26_out, branch_Result, j);
  // Probe on rtype
  // Probe on add_sel
  // Probe on jump_sel
  // Probe on busA_rs
  assign bit_extender_2_out = {{27{1'b0}}, imm16[10:6]};  // Bit_Extender bit_extender_2
  Register #(.width(32)) register_1 (
    .D(multiplexer_15_out), .Q({new_instruction, Jtype26, imm16, funct}), .clk(CLOCK));  // open: en, clr
  Multiplexer #(.width(32)) multiplexer_15 (
    .in0(INSTRUCTION), .in1({32{1'b0}}), .out(multiplexer_15_out), .sel(or_27_out));  // open: en
  or or_27 (or_27_out, or_26_out, or_28_out);
  or or_28 (or_28_out, jr, jal);
  not not_1 (not_1_out, equal);
  // Probe on addu_sel
  // Probe on slt_sel
  LED led_1 (.in(main_2_signed_overflow));
  Multiplexer #(.width(32)) multiplexer_16 (
    .in0(busA_rs), .in1(bit_extender_2_out), .out(multiplexer_16_out), .sel(shamtCtr));  // open: en
  alu_main main_2 (
    .Switch(ALUctl), .X(multiplexer_16_out), .Equal(equal), .Result(main_2_result),
    .Signed_Overflow(main_2_signed_overflow), .Y(multiplexer_14_out));
  // Probe on {new_instruction, Jtype26, imm16, funct}
  or or_29 (branch_Result, and_8_out, and_9_out);
  and and_8 (and_8_out, not_1_out, bne);
  Multiplexer #(.width(4)) multiplexer_17 (.in0(4'b0000), .in1(4'b0001), .out(srl_sel), .sel(srl));  // open: en
  Multiplexer #(.width(4)) multiplexer_18 (.in0(4'b0000), .in1(4'b0010), .out(sra_sel), .sel(sra));  // open: en
  Multiplexer #(.width(4)) multiplexer_19 (.in0(4'b0000), .in1(4'b0101), .out(add_sel), .sel(add_op));  // open: en
  Multiplexer #(.width(4)) multiplexer_20 (.in0(4'b0000), .in1(4'b0110), .out(addu_sel), .sel(addu_op));  // open: en
  Multiplexer #(.width(4)) multiplexer_21 (.in0(4'b0000), .in1(4'b0111), .out(sub_sel), .sel(sub));  // open: en
  Adder #(.width(4)) adder_3 (.a(srl_sel), .b(subu_sel), .out(adder_3_out));  // open: cin, cout
  Adder #(.width(4)) adder_4 (.a(sra_sel), .b(and_sel), .out(adder_4_out));  // open: cin, cout
  Adder #(.width(4)) adder_5 (.a(add_sel), .b(or_sel), .out(adder_5_out));  // open: cin, cout
  Adder #(.width(4)) adder_6 (.a(addu_sel), .b(slt_sel), .out(adder_6_out));  // open: cin, cout
  Adder #(.width(4)) adder_7 (.a(sub_sel), .b(sltu_sel), .out(adder_7_out));  // open: cin, cout
  Adder #(.width(2)) adder_8 (.a(branch_sel), .b(jump_sele), .out(adder_8_out));  // open: cin, cout
  Adder #(.width(3)) adder_9 (.a(lui_sel), .b(megtoreg_sele), .out(adder_9_out));  // open: cin, cout
  Adder #(.width(3)) adder_10 (.a(swinc_sele), .b(jar_sel), .out(adder_10_out));  // open: cin, cout
  Comparator #(.width(6), .mode("unsigned")) comparator_20 (
    .a(funct), .b(6'b101011), .eq(comparator_20_eq));  // open: gt, lt
  Comparator #(.width(6), .mode("unsigned")) comparator_21 (
    .a(funct), .b({6{1'b0}}), .eq(comparator_21_eq));  // open: gt, lt
  Comparator #(.width(6), .mode("unsigned")) comparator_22 (
    .a(funct), .b(6'b000011), .eq(comparator_22_eq));  // open: gt, lt
  Comparator #(.width(6), .mode("unsigned")) comparator_23 (
    .a(funct), .b(6'b000010), .eq(comparator_23_eq));  // open: gt, lt
  Comparator #(.width(6), .mode("unsigned")) comparator_24 (
    .a(new_instruction), .b(6'b101011), .eq(sw));  // open: gt, lt
  Comparator #(.width(6), .mode("unsigned")) comparator_25 (
    .a(new_instruction), .b(6'b101100), .eq(swinc));  // open: gt, lt
  Comparator #(.width(6), .mode("unsigned")) comparator_26 (
    .a(funct), .b(6'b100010), .eq(comparator_26_eq));  // open: gt, lt
  Comparator #(.width(6), .mode("unsigned")) comparator_27 (
    .a(funct), .b(6'b100011), .eq(comparator_27_eq));  // open: gt, lt
  // Probe on sub_sel
  // Probe on sltu_sel
  and and_9 (and_9_out, equal, beq);
  or or_30 (or_30_out, beq, bne);
  or or_31 (or_31_out, or_30_out, or_32_out);
  or or_32 (or_32_out, j, jr);
  Adder #(.width(4)) adder_11 (.a(adder_3_out), .b(adder_4_out), .out(adder_11_out));  // open: cin, cout
  Adder #(.width(4)) adder_12 (.a(adder_5_out), .b(adder_6_out), .out(adder_12_out));  // open: cin, cout
  Adder #(.width(2)) adder_13 (.a(adder_8_out), .b(jr_sele), .out(pc_selector));  // open: cin, cout
  Adder #(.width(3)) adder_14 (.a(adder_9_out), .b(adder_10_out), .out(wb_selector));  // open: cin, cout
  and and_10 (sltu, rtype, comparator_20_eq);
  and and_11 (sll, rtype, comparator_21_eq);
  and and_12 (sra, rtype, comparator_22_eq);
  and and_13 (srl, rtype, comparator_23_eq);
  and and_14 (sub, rtype, comparator_26_eq);
  and and_15 (subu, rtype, comparator_27_eq);
  // Probe on subu_sel
  // Probe on srl_sel
  not not_2 (RegWr, or_33_out);
  or or_33 (or_33_out, or_31_out, sw);
  Multiplexer #(.width(4)) multiplexer_22 (.in0(4'b0000), .in1(4'b1000), .out(subu_sel), .sel(subu));  // open: en
  Multiplexer #(.width(4)) multiplexer_23 (.in0(4'b0000), .in1(4'b1001), .out(and_sel), .sel(and_op));  // open: en
  Multiplexer #(.width(4)) multiplexer_24 (.in0(4'b0000), .in1(4'b1010), .out(or_sel), .sel(or_op));  // open: en
  Multiplexer #(.width(4)) multiplexer_25 (.in0(4'b0000), .in1(4'b1011), .out(slt_sel), .sel(slt_op));  // open: en
  Multiplexer #(.width(4)) multiplexer_26 (.in0(4'b0000), .in1(4'b1100), .out(sltu_sel), .sel(sltu_op));  // open: en
  Adder #(.width(4)) adder_15 (.a(adder_11_out), .b(adder_12_out), .out(adder_15_out));  // open: cin, cout
  // Probe on and_sel
  // Probe on sw
  // Probe on sra_sel
  // mem_main main_3: pin names not known; wires that end beside it: main_2_result, busb, MemWr, CLOCK, main_3_p5
  // Probe on ALUctl
  Adder #(.width(4)) adder_16 (.a(adder_15_out), .b(adder_7_out), .out(ALUctl));  // open: cin, cout
  // Probe on or_sel
  // Probe on beq
  // Probe on lw
  // Probe on imm_after_shift
  Multiplier #(.width(32)) multiplier_1 (
    .a({imm_ext, imm16, funct}), .b(32'h4), .out(imm_after_shift));  // open: cin, cout
  Adder #(.width(32)) adder_17 (.a(imm_after_shift), .b(FETCH_ADDRESS), .out(imm_result));  // open: cin, cout
  // Probe on bne
  Multiplexer #(.select(3), .width(32)) multiplexer_27 (
    .in0(main_2_result), .in1(upper), .in2(main_3_p5), .in3(swinc_rs_imm16), .in4(FETCH_ADDRESS),
    .out(multiplexer_27_out), .sel(wb_selector));  // open: in5, in6, in7, en
  // Probe on imm_result

  // Other names for the same wires on the sheet: clk = CLOCK; fetch_addr[31:0] = FETCH_ADDRESS; imm16[5:0] = funct;
  //   imm_ext[15:0] = {imm16, funct}; Jtype26[15:0] = {imm16, funct}; jump_addr[27:2] = {Jtype26, imm16, funct};
  //   new_instruction[25:0] = {Jtype26, imm16, funct}; pc_4[31:28] = jump_addr; MemtoReg = lw;
  //   opcode[5:0] = new_instruction; ra[31:0] = ra_Value; rd[4:0] = imm16[15:11]; imm16_topbit = imm16[15];
  //   rs[4:0] = Jtype26[25:21]; rt[4:0] = Jtype26[20:16]; s0[31:0] = s0_Value; s1[31:0] = s1_Value;
  //   s2[31:0] = s2_Value; shamt[4:0] = imm16[10:6]; sp[31:0] = sp_Value

  // Notes on the sheet:
  //   busW
  //   Output
  //   These are outputs/inputs from run.circ
  //   Inputs
  //   busA
  //   busB
  //   These are DEBUG/TEST outputs from your circuit.
endmodule
