// Logisim project alu.circ as structural Verilog: 1 circuit, main circuit main
// 2
module main (
  input  [31:0] X,
  input  [31:0] Y,
  input  [3:0] Switch,
  output Signed_Overflow,
  output Equal,
  output [31:0] Result
);

  wire and_2_out, and_3_out, and_4_out, and_5_out, not_1_out, not_2_out, not_3_out, not_4_out, not_5_out,
       not_6_out, or_2_out, or_3_out, slt, sltu;
  wire [4:0] bit_extender_1_out, bit_extender_2_out, bit_extender_3_out;
  wire [31:0] add, addu, \and , bit_extender_4_out, bit_extender_5_out, \or , sll, sra, srl, sub, subu;

  Bit_Extender #(.in_width(32), .out_width(5)) bit_extender_1 (.in(X), .out(bit_extender_1_out));
  Adder #(.width(32)) adder_1 (.a(X), .b(Y), .out(addu));  // open: cin, cout
  Subtractor #(.width(32)) subtractor_1 (.a(X), .b(Y), .out(subu));  // open: bin, bout
  Adder #(.width(32)) adder_2 (.a(X), .b(Y), .out(add));  // open: cin, cout
  Subtractor #(.width(32)) subtractor_2 (.a(X), .b(Y), .out(sub));  // open: bin, bout
  Shifter #(.width(32)) shifter_1 (.in(Y), .\dist (bit_extender_1_out), .out(sll));
  Bit_Extender #(.in_width(32), .out_width(5)) bit_extender_2 (.in(X), .out(bit_extender_2_out));
  assign \and  = X & Y;  // AND_Gate and_1, 32 bits wide
  Comparator #(.width(32)) comparator_1 (.a(X), .b(Y), .eq(Equal), .lt(slt));  // open: gt
  Shifter #(.width(32), .shift("lr")) shifter_2 (.in(Y), .\dist (bit_extender_2_out), .out(srl));
  and and_2 (and_2_out, X[31], Y[31], not_1_out);
  not not_1 (not_1_out, add[31]);
  not not_2 (not_2_out, X[31]);
  not not_3 (not_3_out, Y[31]);
  and and_3 (and_3_out, not_2_out, not_3_out, add[31]);
  not not_4 (not_4_out, X[31]);
  and and_4 (and_4_out, not_4_out, Y[31], sub[31]);
  and and_5 (and_5_out, X[31], not_5_out, not_6_out);
  not not_5 (not_5_out, Y[31]);
  not not_6 (not_6_out, sub[31]);
  assign \or  = X | Y;  // OR_Gate or_1, 32 bits wide
  Comparator #(.width(32), .mode("unsigned")) comparator_2 (.a(X), .b(Y), .lt(sltu));  // open: gt, eq
  or or_2 (or_2_out, and_2_out, and_3_out);
  or or_3 (or_3_out, and_4_out, and_5_out);
  Shifter #(.width(32), .shift("ar")) shifter_3 (.in(Y), .\dist (bit_extender_3_out), .out(sra));
  Bit_Extender #(.in_width(32), .out_width(5)) bit_extender_3 (.in(X), .out(bit_extender_3_out));
  Multiplexer #(.select(4)) multiplexer_1 (
    .in0(1'b0), .in1(1'b0), .in2(1'b0), .in5(or_2_out), .in6(1'b0), .in7(or_3_out), .in8(1'b0), .in9(1'b0),
    .in10(1'b0), .in11(1'b0), .in12(1'b0), .out(Signed_Overflow), .sel(Switch));  // open: in3, in4, in13, in14, in15, en
  assign bit_extender_4_out = {{31{1'b0}}, slt};  // Bit_Extender bit_extender_4
  assign bit_extender_5_out = {{31{1'b0}}, sltu};  // Bit_Extender bit_extender_5
  Multiplexer #(.select(4), .width(32)) multiplexer_2 (
    .in0(sll), .in1(srl), .in2(sra), .in5(add), .in6(addu), .in7(sub), .in8(subu), .in9(\and ), .in10(\or ),
    .in11(bit_extender_4_out), .in12(bit_extender_5_out), .out(Result), .sel(Switch));  // open: in3, in4, in13, in14, in15, en

  // Other names for the same wires on the sheet: overflow = Signed_Overflow; S[3:0] = Switch

  // Notes on the sheet:
  //   INPUTS to your circuit
  //   DON'T CHANGE THE LOCATIONS OF THE INPUTS AND OUTPUTS!
  //   OUTPUTS from your circuit
endmodule
