// Logisim project regfile.circ as structural Verilog: 1 circuit, main circuit main
module main (
  input  [4:0] Read_Register_1,
  input  [4:0] Read_Register_2,
  input  [4:0] Write_Register,
  input  [31:0] Write_Data,
  input  Write_Enable,
  input  Clock,
  output [31:0] s0_Value,
  output [31:0] s1_Value,
  output [31:0] s2_Value,
  output [31:0] ra_Value,
  output [31:0] sp_Value,
  output [31:0] Read_Data_1,
  output [31:0] Read_Data_2
);

  wire a0_en, a1_en, a2_en, a3_en, at_en, fp_en, gp_en, k0_en, k1_en, ra_en, s0_en, s1_en, s2_en, s3_en,
       s4_en, s5_en, s6_en, s7_en, sp_en, t0_en, t1_en, t2_en, t3_en, t4_en, t5_en, t6_en, t7_en, t8_en,
       t9_en, v0_en, v1_en;
  wire [31:0] a0_in, a0_out, a1_in, a1_out, a2_in, a2_out, a3_in, a3_out, at_in, at_out, fp_in, fp_out,
       gp_in, gp_out, k0_in, k0_out, k1_in, k1_out, ra_in, s0_in, s1_in, s2_in, s3_in, s3_out, s4_in, s4_out,
       s5_in, s5_out, s6_in, s6_out, s7_in, s7_out, sp_in, t0_in, t0_out, t1_in, t1_out, t2_in, t2_out,
       t3_in, t3_out, t4_in, t4_out, t5_in, t5_out, t6_in, t6_out, t7_in, t7_out, t8_in, t8_out, t9_in,
       t9_out, v0_in, v0_out, v1_in, v1_out;

  Register #(.width(32)) register_1 (.D(t6_in), .en(t6_en), .Q(t6_out), .clk(Clock));  // open: clr
  Register #(.width(32)) register_2 (.D(s5_in), .en(s5_en), .Q(s5_out), .clk(Clock));  // open: clr
  Register #(.width(32)) register_3 (.D(gp_in), .en(gp_en), .Q(gp_out), .clk(Clock));  // open: clr
  Register #(.width(32)) register_4 (.D(t7_in), .en(t7_en), .Q(t7_out), .clk(Clock));  // open: clr
  Register #(.width(32)) register_5 (.D(s6_in), .en(s6_en), .Q(s6_out), .clk(Clock));  // open: clr
  Register #(.width(32)) register_6 (.D(sp_in), .en(sp_en), .Q(sp_Value), .clk(Clock));  // open: clr
  Multiplexer #(.select(5), .width(32)) multiplexer_1 (
    .in0({32{1'b0}}), .in1(at_out), .in2(v0_out), .in3(v1_out), .in4(a0_out), .in5(a1_out), .in6(a2_out),
    .in7(a3_out), .in8(t0_out), .in9(t1_out), .in10(t2_out), .in11(t3_out), .in12(t4_out), .in13(t5_out),
    .in14(t6_out), .in15(t7_out), .in16(s0_Value), .in17(s1_Value), .in18(s2_Value), .in19(s3_out),
    .in20(s4_out), .in21(s5_out), .in22(s6_out), .in23(s7_out), .in24(t8_out), .in25(t9_out), .in26(k0_out),
    .in27(k1_out), .in28(gp_out), .in29(sp_Value), .in30(fp_out), .in31(ra_Value), .out(Read_Data_1),
    .sel(Read_Register_1));  // open: en
  Register #(.width(32)) register_7 (.D(v1_in), .en(v1_en), .Q(v1_out), .clk(Clock));  // open: clr
  Register #(.width(32)) register_8 (.D(a2_in), .en(a2_en), .Q(a2_out), .clk(Clock));  // open: clr
  Register #(.width(32)) register_9 (.D(t2_in), .en(t2_en), .Q(t2_out), .clk(Clock));  // open: clr
  Register #(.width(32)) register_10 (.D(s0_in), .en(s0_en), .Q(s0_Value), .clk(Clock));  // open: clr
  Register #(.width(32)) register_11 (.D(s7_in), .en(s7_en), .Q(s7_out), .clk(Clock));  // open: clr
  Register #(.width(32)) register_12 (.D(fp_in), .en(fp_en), .Q(fp_out), .clk(Clock));  // open: clr
  Register #(.width(32)) register_13 (.D(at_in), .en(at_en), .Q(at_out), .clk(Clock));  // open: clr
  Register #(.width(32)) register_14 (.D(a0_in), .en(a0_en), .Q(a0_out), .clk(Clock));  // open: clr
  Register #(.width(32)) register_15 (.D(a3_in), .en(a3_en), .Q(a3_out), .clk(Clock));  // open: clr
  Register #(.width(32)) register_16 (.D(t3_in), .en(t3_en), .Q(t3_out), .clk(Clock));  // open: clr
  Register #(.width(32)) register_17 (.D(s1_in), .en(s1_en), .Q(s1_Value), .clk(Clock));  // open: clr
  Register #(.width(32)) register_18 (.D(t8_in), .en(t8_en), .Q(t8_out), .clk(Clock));  // open: clr
  Register #(.width(32)) register_19 (.D(ra_in), .en(ra_en), .Q(ra_Value), .clk(Clock));  // open: clr
  Register #(.width(32)) register_20 (.D(v0_in), .en(v0_en), .Q(v0_out), .clk(Clock));  // open: clr
  Register #(.width(32)) register_21 (.D(a1_in), .en(a1_en), .Q(a1_out), .clk(Clock));  // open: clr
  Register #(.width(32)) register_22 (.D(t0_in), .en(t0_en), .Q(t0_out), .clk(Clock));  // open: clr
  Register #(.width(32)) register_23 (.D(t4_in), .en(t4_en), .Q(t4_out), .clk(Clock));  // open: clr
  Multiplexer #(.select(5), .width(32)) multiplexer_2 (
    .in0({32{1'b0}}), .in1(at_out), .in2(v0_out), .in3(v1_out), .in4(a0_out), .in5(a1_out), .in6(a2_out),
    .in7(a3_out), .in8(t0_out), .in9(t1_out), .in10(t2_out), .in11(t3_out), .in12(t4_out), .in13(t5_out),
    .in14(t6_out), .in15(t7_out), .in16(s0_Value), .in17(s1_Value), .in18(s2_Value), .in19(s3_out),
    .in20(s4_out), .in21(s5_out), .in22(s6_out), .in23(s7_out), .in24(t8_out), .in25(t9_out), .in26(k0_out),
    .in27(k1_out), .in28(gp_out), .in29(sp_Value), .in30(fp_out), .in31(ra_Value), .out(Read_Data_2),
    .sel(Read_Register_2));  // open: en
  Register #(.width(32)) register_24 (.D(s2_in), .en(s2_en), .Q(s2_Value), .clk(Clock));  // open: clr
  Register #(.width(32)) register_25 (.D(t9_in), .en(t9_en), .Q(t9_out), .clk(Clock));  // open: clr
  Register #(.width(32)) register_26 (.D(t1_in), .en(t1_en), .Q(t1_out), .clk(Clock));  // open: clr
  Register #(.width(32)) register_27 (.D(t5_in), .en(t5_en), .Q(t5_out), .clk(Clock));  // open: clr
  Register #(.width(32)) register_28 (.D(s3_in), .en(s3_en), .Q(s3_out), .clk(Clock));  // open: clr
  Register #(.width(32)) register_29 (.D(k0_in), .en(k0_en), .Q(k0_out), .clk(Clock));  // open: clr
  Demultiplexer #(.select(5), .width(32)) demultiplexer_1 (
    .out1(at_in), .out2(v0_in), .out3(v1_in), .out4(a0_in), .out5(a1_in), .out6(a2_in), .out7(a3_in),
    .out8(t0_in), .out9(t1_in), .out10(t2_in), .out11(t3_in), .out12(t4_in), .out13(t5_in), .out14(t6_in),
    .out15(t7_in), .out16(s0_in), .out17(s1_in), .out18(s2_in), .out19(s3_in), .out20(s4_in), .out21(s5_in),
    .out22(s6_in), .out23(s7_in), .out24(t8_in), .out25(t9_in), .out26(k0_in), .out27(k1_in), .out28(gp_in),
    .out29(sp_in), .out30(fp_in), .out31(ra_in), .in(Write_Data), .sel(Write_Register));  // open: out0, en
  Register #(.width(32)) register_30 (.D(s4_in), .en(s4_en), .Q(s4_out), .clk(Clock));  // open: clr
  Register #(.width(32)) register_31 (.D(k1_in), .en(k1_en), .Q(k1_out), .clk(Clock));  // open: clr
  Demultiplexer #(.select(5)) demultiplexer_2 (
    .out1(at_en), .out2(v0_en), .out3(v1_en), .out4(a0_en), .out5(a1_en), .out6(a2_en), .out7(a3_en),
    .out8(t0_en), .out9(t1_en), .out10(t2_en), .out11(t3_en), .out12(t4_en), .out13(t5_en), .out14(t6_en),
    .out15(t7_en), .out16(s0_en), .out17(s1_en), .out18(s2_en), .out19(s3_en), .out20(s4_en), .out21(s5_en),
    .out22(s6_en), .out23(s7_en), .out24(t8_en), .out25(t9_en), .out26(k0_en), .out27(k1_en), .out28(gp_en),
    .out29(sp_en), .out30(fp_en), .out31(ra_en), .in(Write_Enable), .sel(Write_Register));  // open: out0, en

  // Other names for the same wires on the sheet: clk = Clock; ra_out[31:0] = ra_Value; read_data1[31:0] = Read_Data_1;
  //   read_data2[31:0] = Read_Data_2; read_reg1[4:0] = Read_Register_1; read_reg2[4:0] = Read_Register_2;
  //   s0_out[31:0] = s0_Value; s1_out[31:0] = s1_Value; s2_out[31:0] = s2_Value; sp_out[31:0] = sp_Value;
  //   write_en = Write_Enable; write_reg[4:0] = Write_Register

  // Notes on the sheet:
  //   INPUTS to your circuit
  //   $t6
  //   $s5
  //   $gp
  //   DON'T CHANGE THE LOCATIONS OF THE INPUTS AND OUTPUTS!
  //   $t7
  //   $s6
  //   $sp
  //   Read1
  //   $v1
  //   $a2
  //   $t2
  //   $s0
  //   $s7
  //   $fp
  //   $at
  //   $a0
  //   $a3
  //   $t3
  //   These are DEBUG/TEST outputs from your circuit.
  //   $s1
  //   $t8
  //   $ra
  //   $v0
  //   $a1
  //   $t0
  //   $t4
  //   Read2
  //   $s2
  //   $t9
  //   $t1
  //   $t5
  //   $s3
  //   $k0
  //   write
  //   OUTPUTS from your circuit
  //   $s4
  //   $k1
  //   write
endmodule
